// Logisim project 02_multiplexador_4x1.circ as structural Verilog: 1 circuit, main circuit main
module main (
  input  A,
  input  B,
  input  C,
  input  D,
  input  C0,
  input  C1,
  output S
);

  wire and_1_out, and_2_out, and_3_out, and_4_out, or_1_out;

  and and_1 (and_1_out, A, ~C0, ~C1);  // AND_Gate
  and and_2 (and_2_out, B, ~C0, C1);  // AND_Gate
  and and_3 (and_3_out, C, C0, ~C1);  // AND_Gate
  and and_4 (and_4_out, D, C0, C1);
  or or_1 (or_1_out, and_1_out, and_2_out, and_3_out, and_4_out);
  buf and_5 (S, or_1_out);  // AND_Gate
endmodule
