// Logisim project 05_memoriaROM.circ as structural Verilog: 6 circuits, main circuit main
module main (
  input  [2:0] CHAVE,
  output [7:0] SAIDA
);

  multiplex8x1_8bits multiplex8x1_8bits_1 (
    .A0(8'h1), .A1(8'h3), .A2(8'he), .A3(8'h11), .A4(8'h8), .A5(8'h1d), .A6(8'ha), .A7(8'h19), .chave(CHAVE),
    .SAIDA(SAIDA));
endmodule

module multiplex4x1_8bits (
  input  [7:0] in_1,
  input  [7:0] in_2,
  input  [1:0] chave,
  input  [7:0] in_4,
  input  [7:0] in_5,
  output [7:0] S
);

  multiplex4x1 multiplex4x1_1 (
    .in_1(in_1[0]), .in_2(in_2[0]), .in_3(in_4[0]), .in_4(in_5[0]), .S2(chave[1]), .S1(chave[0]), .out_7(S[0]));
  multiplex4x1 multiplex4x1_2 (
    .in_1(in_1[1]), .in_2(in_2[1]), .in_3(in_4[1]), .in_4(in_5[1]), .S2(chave[1]), .S1(chave[0]), .out_7(S[1]));
  multiplex4x1 multiplex4x1_3 (
    .in_1(in_1[2]), .in_2(in_2[2]), .in_3(in_4[2]), .in_4(in_5[2]), .S2(chave[1]), .S1(chave[0]), .out_7(S[2]));
  multiplex4x1 multiplex4x1_4 (
    .in_1(in_1[3]), .in_2(in_2[3]), .in_3(in_4[3]), .in_4(in_5[3]), .S2(chave[1]), .S1(chave[0]), .out_7(S[3]));
  multiplex4x1 multiplex4x1_5 (
    .in_1(in_1[4]), .in_2(in_2[4]), .in_3(in_4[4]), .in_4(in_5[4]), .S2(chave[1]), .S1(chave[0]), .out_7(S[4]));
  multiplex4x1 multiplex4x1_6 (
    .in_1(in_1[5]), .in_2(in_2[5]), .in_3(in_4[5]), .in_4(in_5[5]), .S2(chave[1]), .S1(chave[0]), .out_7(S[5]));
  multiplex4x1 multiplex4x1_7 (
    .in_1(in_1[6]), .in_2(in_2[6]), .in_3(in_4[6]), .in_4(in_5[6]), .S2(chave[1]), .S1(chave[0]), .out_7(S[6]));
  multiplex4x1 multiplex4x1_8 (
    .in_1(in_1[7]), .in_2(in_2[7]), .in_3(in_4[7]), .in_4(in_5[7]), .S2(chave[1]), .S1(chave[0]), .out_7(S[7]));
endmodule

module multiplex4x1 (
  input  in_1,
  input  in_2,
  input  in_3,
  input  in_4,
  input  S2,
  input  S1,
  output out_7
);

  wire and_1_out, and_2_out, and_3_out, and_4_out;

  and and_1 (and_1_out, in_1, ~S2, ~S1);  // AND_Gate
  and and_2 (and_2_out, in_2, ~S2, S1);  // AND_Gate
  and and_3 (and_3_out, in_3, S2, ~S1);  // AND_Gate
  and and_4 (and_4_out, in_4, S2, S1);
  or or_1 (out_7, and_1_out, and_2_out, and_3_out, and_4_out);
endmodule

// MUX2x1
module multiplex2x1 (
  input  A,
  input  B,
  input  chave,
  output S
);

  wire and_1_out, and_2_out, not_1_out;

  and and_1 (and_1_out, A, not_1_out);
  not not_1 (not_1_out, chave);
  and and_2 (and_2_out, B, chave);
  or or_1 (S, and_1_out, and_2_out);
endmodule

module multiplex2x1_8bits (
  input  [7:0] E1,
  input  [7:0] E2,
  input  chave,
  output [7:0] S
);

  multiplex2x1 multiplex2x1_1 (.A(E1[0]), .B(E2[0]), .S(S[0]), .chave(chave));
  multiplex2x1 multiplex2x1_2 (.A(E1[1]), .B(E2[1]), .S(S[1]), .chave(chave));
  multiplex2x1 multiplex2x1_3 (.A(E1[2]), .B(E2[2]), .S(S[2]), .chave(chave));
  multiplex2x1 multiplex2x1_4 (.A(E1[3]), .B(E2[3]), .S(S[3]), .chave(chave));
  multiplex2x1 multiplex2x1_5 (.A(E1[4]), .B(E2[4]), .S(S[4]), .chave(chave));
  multiplex2x1 multiplex2x1_6 (.A(E1[5]), .B(E2[5]), .S(S[5]), .chave(chave));
  multiplex2x1 multiplex2x1_7 (.A(E1[6]), .B(E2[6]), .S(S[6]), .chave(chave));
  multiplex2x1 multiplex2x1_8 (.A(E1[7]), .B(E2[7]), .S(S[7]), .chave(chave));
endmodule

module multiplex8x1_8bits (
  input  [7:0] A0,
  input  [7:0] A1,
  input  [7:0] A2,
  input  [7:0] A3,
  input  [7:0] A4,
  input  [7:0] A5,
  input  [7:0] A6,
  input  [7:0] A7,
  input  [2:0] chave,
  output [7:0] SAIDA
);

  wire [7:0] multiplex4x1_8bits_1_s, multiplex4x1_8bits_2_s;

  multiplex4x1_8bits multiplex4x1_8bits_1 (
    .in_1(A0), .in_2(A1), .chave(chave[1:0]), .in_4(A2), .in_5(A3), .S(multiplex4x1_8bits_1_s));
  multiplex4x1_8bits multiplex4x1_8bits_2 (
    .in_1(A4), .in_2(A5), .chave(chave[1:0]), .in_4(A6), .in_5(A7), .S(multiplex4x1_8bits_2_s));
  multiplex2x1_8bits multiplex2x1_8bits_1 (
    .E1(multiplex4x1_8bits_1_s), .E2(multiplex4x1_8bits_2_s), .chave(chave[2]), .S(SAIDA));
endmodule
