// Logisim project 07_banco_registradores.circ as structural Verilog: 9 circuits, main circuit registrador-8-bits
module registrador_8_bits (
  input  SET,
  input  CLOCK,
  input  RESET,
  input  [7:0] ENTRADA,
  output [7:0] out_5
);

  FLIPFLOP_D flipflop_d_1 (.T(ENTRADA[0]), .CLOCK(CLOCK), .Q(out_5[0]), .SET(SET), .RESET(RESET));  // open: nQ
  FLIPFLOP_D flipflop_d_2 (.T(ENTRADA[1]), .CLOCK(CLOCK), .Q(out_5[1]), .SET(SET), .RESET(RESET));  // open: nQ
  FLIPFLOP_D flipflop_d_3 (.T(ENTRADA[2]), .CLOCK(CLOCK), .Q(out_5[2]), .SET(SET), .RESET(RESET));  // open: nQ
  FLIPFLOP_D flipflop_d_4 (.T(ENTRADA[3]), .CLOCK(CLOCK), .Q(out_5[3]), .SET(SET), .RESET(RESET));  // open: nQ
  FLIPFLOP_D flipflop_d_5 (.T(ENTRADA[4]), .CLOCK(CLOCK), .Q(out_5[4]), .SET(SET), .RESET(RESET));  // open: nQ
  FLIPFLOP_D flipflop_d_6 (.T(ENTRADA[5]), .CLOCK(CLOCK), .Q(out_5[5]), .SET(SET), .RESET(RESET));  // open: nQ
  FLIPFLOP_D flipflop_d_7 (.T(ENTRADA[6]), .CLOCK(CLOCK), .Q(out_5[6]), .SET(SET), .RESET(RESET));  // open: nQ
  FLIPFLOP_D flipflop_d_8 (.T(ENTRADA[7]), .CLOCK(CLOCK), .Q(out_5[7]), .SET(SET), .RESET(RESET));  // open: nQ
endmodule

module FLIPFLOP_D (
  input  SET,
  input  T,
  input  CLOCK,
  input  RESET,
  output Q,
  output nQ
);

  wire nand_1_out, nand_2_out, nand_3_out, nand_4_out, nand_5_out, nand_6_out, not_1_out, not_2_out,
       not_3_out, not_4_out, not_5_out;

  not not_1 (not_1_out, CLOCK);
  not not_2 (not_2_out, T);
  nand nand_1 (nand_1_out, nQ, T, not_1_out);
  nand nand_2 (nand_2_out, not_1_out, not_2_out, Q);
  not not_3 (not_3_out, SET);
  not not_4 (not_4_out, RESET);
  nand nand_3 (nand_3_out, not_3_out, nand_1_out, nand_4_out);
  not not_5 (not_5_out, not_1_out);
  nand nand_4 (nand_4_out, nand_3_out, nand_2_out, not_4_out);
  nand nand_5 (nand_5_out, nand_3_out, not_4_out, not_5_out);
  nand nand_6 (nand_6_out, not_5_out, not_3_out, nand_4_out);
  nand nand_7 (Q, not_3_out, nand_5_out, nQ);
  nand nand_8 (nQ, Q, nand_6_out, not_4_out);
endmodule

module banco_registradores (
  input  RESET,
  input  SET,
  input  [2:0] in_3,
  input  [7:0] in_4,
  input  in_5,
  input  [2:0] in_6,
  input  CLOCK,
  input  in_8,
  input  in_9,
  input  [2:0] in_10,
  output [7:0] out_11,
  output [7:0] out_12
);

  wire demultiplexador_1_out_4, demultiplexador_1_out_5, demultiplexador_1_out_6, demultiplexador_1_out_7,
       demultiplexador_1_out_8, demultiplexador_1_out_9, demultiplexador_1_out_10, demultiplexador_1_out_11;
  wire [7:0] registrador_8_bits_1_out_5, registrador_8_bits_2_out_5, registrador_8_bits_3_out_5,
       registrador_8_bits_4_out_5, registrador_8_bits_5_out_5, registrador_8_bits_6_out_5,
       registrador_8_bits_7_out_5, registrador_8_bits_8_out_5;

  demultiplexador demultiplexador_1 (
    .CLOCK(CLOCK), .in_3(in_10), .out_4(demultiplexador_1_out_4), .out_5(demultiplexador_1_out_5),
    .out_6(demultiplexador_1_out_6), .out_7(demultiplexador_1_out_7), .out_8(demultiplexador_1_out_8),
    .out_9(demultiplexador_1_out_9), .out_10(demultiplexador_1_out_10), .out_11(demultiplexador_1_out_11),
    .LOAD(in_8));
  registrador_8_bits registrador_8_bits_1 (
    .out_5(registrador_8_bits_1_out_5), .SET(SET), .RESET(RESET), .CLOCK(demultiplexador_1_out_4),
    .ENTRADA(in_4));
  registrador_8_bits registrador_8_bits_2 (
    .out_5(registrador_8_bits_2_out_5), .SET(SET), .RESET(RESET), .CLOCK(demultiplexador_1_out_6),
    .ENTRADA(in_4));
  registrador_8_bits registrador_8_bits_3 (
    .out_5(registrador_8_bits_3_out_5), .SET(SET), .RESET(RESET), .CLOCK(demultiplexador_1_out_8),
    .ENTRADA(in_4));
  registrador_8_bits registrador_8_bits_4 (
    .out_5(registrador_8_bits_4_out_5), .SET(SET), .RESET(RESET), .CLOCK(demultiplexador_1_out_10),
    .ENTRADA(in_4));
  registrador_8_bits registrador_8_bits_5 (
    .out_5(registrador_8_bits_5_out_5), .SET(SET), .RESET(RESET), .CLOCK(demultiplexador_1_out_5),
    .ENTRADA(in_4));
  registrador_8_bits registrador_8_bits_6 (
    .out_5(registrador_8_bits_6_out_5), .SET(SET), .RESET(RESET), .CLOCK(demultiplexador_1_out_7),
    .ENTRADA(in_4));
  registrador_8_bits registrador_8_bits_7 (
    .out_5(registrador_8_bits_7_out_5), .SET(SET), .RESET(RESET), .CLOCK(demultiplexador_1_out_9),
    .ENTRADA(in_4));
  registrador_8_bits registrador_8_bits_8 (
    .out_5(registrador_8_bits_8_out_5), .SET(SET), .RESET(RESET), .CLOCK(demultiplexador_1_out_11),
    .ENTRADA(in_4));
  multiplexador8x1_8bits multiplexador8x1_8bits_1 (
    .in_1(registrador_8_bits_1_out_5), .in_2(registrador_8_bits_5_out_5), .in_3(registrador_8_bits_2_out_5),
    .in_4(registrador_8_bits_6_out_5), .in_5(registrador_8_bits_3_out_5), .in_6(registrador_8_bits_7_out_5),
    .in_7(registrador_8_bits_4_out_5), .in_8(registrador_8_bits_8_out_5), .in_10(in_3), .out_11(out_11),
    .load(in_5));
  multiplexador8x1_8bits multiplexador8x1_8bits_2 (
    .in_1(registrador_8_bits_1_out_5), .in_2(registrador_8_bits_5_out_5), .in_3(registrador_8_bits_2_out_5),
    .in_4(registrador_8_bits_6_out_5), .in_5(registrador_8_bits_3_out_5), .in_6(registrador_8_bits_7_out_5),
    .in_7(registrador_8_bits_4_out_5), .in_8(registrador_8_bits_8_out_5), .in_10(in_6), .out_11(out_12),
    .load(in_9));
endmodule

module demultiplexador (
  input  LOAD,
  input  CLOCK,
  input  [2:0] in_3,
  output out_4,
  output out_5,
  output out_6,
  output out_7,
  output out_8,
  output out_9,
  output out_10,
  output out_11
);

  wire and_1_out, not_1_out, not_2_out, not_3_out, not_4_out, not_5_out, not_6_out, not_7_out, not_8_out,
       not_9_out, not_10_out, not_11_out, not_12_out;

  and and_1 (and_1_out, LOAD, CLOCK);
  not not_1 (not_1_out, in_3[2]);
  not not_2 (not_2_out, in_3[1]);
  not not_3 (not_3_out, in_3[0]);
  not not_4 (not_4_out, in_3[2]);
  not not_5 (not_5_out, in_3[1]);
  not not_6 (not_6_out, in_3[2]);
  not not_7 (not_7_out, in_3[0]);
  not not_8 (not_8_out, in_3[2]);
  not not_9 (not_9_out, in_3[1]);
  not not_10 (not_10_out, in_3[0]);
  not not_11 (not_11_out, in_3[1]);
  not not_12 (not_12_out, in_3[0]);
  and _0 (out_4, and_1_out, not_1_out, not_2_out, not_3_out);
  and _1 (out_5, and_1_out, not_4_out, not_5_out, in_3[0]);
  and _2 (out_6, and_1_out, not_6_out, in_3[1], not_7_out);
  and _3 (out_7, and_1_out, not_8_out, in_3[1], in_3[0]);
  and _4 (out_8, and_1_out, in_3[2], not_9_out, not_10_out);
  and _5 (out_9, and_1_out, in_3[2], not_11_out, in_3[0]);
  and _6 (out_10, and_1_out, in_3[2], in_3[1], not_12_out);
  and _7 (out_11, and_1_out, in_3[2], in_3[1], in_3[0]);
endmodule

module multiplexador_4x1 (
  input  in_1,
  input  in_2,
  input  in_3,
  input  LOAD,
  input  in_5,
  input  in_6,
  input  in_7,
  output out_8
);

  wire and_1_out, and_2_out, and_3_out, and_4_out, or_1_out;

  and and_1 (and_1_out, in_1, ~in_6, ~in_7);  // AND_Gate
  and and_2 (and_2_out, in_2, ~in_6, in_7);  // AND_Gate
  and and_3 (and_3_out, in_3, in_6, ~in_7);  // AND_Gate
  and and_4 (and_4_out, in_5, in_6, in_7);
  or or_1 (or_1_out, and_1_out, and_2_out, and_3_out, and_4_out);
  and and_5 (out_8, or_1_out, LOAD);
endmodule

module multiplexador_4x1_8bits (
  input  [7:0] in_1,
  input  [7:0] in_2,
  input  [7:0] in_3,
  input  [1:0] in_4,
  input  [7:0] in_5,
  input  in_6,
  output [7:0] out_7
);

  multiplexador_4x1 multiplexador_4x1_1 (
    .in_1(in_1[0]), .in_2(in_2[0]), .in_3(in_3[0]), .in_5(in_5[0]), .in_6(in_4[1]), .in_7(in_4[0]),
    .out_8(out_7[0]), .LOAD(in_6));
  multiplexador_4x1 multiplexador_4x1_2 (
    .in_1(in_1[1]), .in_2(in_2[1]), .in_3(in_3[1]), .in_5(in_5[1]), .in_6(in_4[1]), .in_7(in_4[0]),
    .out_8(out_7[1]), .LOAD(in_6));
  multiplexador_4x1 multiplexador_4x1_3 (
    .in_1(in_1[2]), .in_2(in_2[2]), .in_3(in_3[2]), .in_5(in_5[2]), .in_6(in_4[1]), .in_7(in_4[0]),
    .out_8(out_7[2]), .LOAD(in_6));
  multiplexador_4x1 multiplexador_4x1_4 (
    .in_1(in_1[3]), .in_2(in_2[3]), .in_3(in_3[3]), .in_5(in_5[3]), .in_6(in_4[1]), .in_7(in_4[0]),
    .out_8(out_7[3]), .LOAD(in_6));
  multiplexador_4x1 multiplexador_4x1_5 (
    .in_1(in_1[4]), .in_2(in_2[4]), .in_3(in_3[4]), .in_5(in_5[4]), .in_6(in_4[1]), .in_7(in_4[0]),
    .out_8(out_7[4]), .LOAD(in_6));
  multiplexador_4x1 multiplexador_4x1_6 (
    .in_1(in_1[5]), .in_2(in_2[5]), .in_3(in_3[5]), .in_5(in_5[5]), .in_6(in_4[1]), .in_7(in_4[0]),
    .out_8(out_7[5]), .LOAD(in_6));
  multiplexador_4x1 multiplexador_4x1_7 (
    .in_1(in_1[6]), .in_2(in_2[6]), .in_3(in_3[6]), .in_5(in_5[6]), .in_6(in_4[1]), .in_7(in_4[0]),
    .out_8(out_7[6]), .LOAD(in_6));
  multiplexador_4x1 multiplexador_4x1_8 (
    .in_1(in_1[7]), .in_2(in_2[7]), .in_3(in_3[7]), .in_5(in_5[7]), .in_6(in_4[1]), .in_7(in_4[0]),
    .out_8(out_7[7]), .LOAD(in_6));
endmodule

module multiplexador8x1_8bits (
  input  [7:0] in_1,
  input  [7:0] in_2,
  input  [7:0] in_3,
  input  [7:0] in_4,
  input  [7:0] in_5,
  input  [7:0] in_6,
  input  [7:0] in_7,
  input  [7:0] in_8,
  input  load,
  input  [2:0] in_10,
  output [7:0] out_11
);

  wire [7:0] multiplexador_4x1_8bits_1_out_7, multiplexador_4x1_8bits_2_out_7;

  multiplexador_4x1_8bits multiplexador_4x1_8bits_1 (
    .in_1(in_1), .in_2(in_2), .in_3(in_3), .in_4(in_10[1:0]), .in_5(in_4),
    .out_7(multiplexador_4x1_8bits_1_out_7), .in_6(load));
  multiplexador_4x1_8bits multiplexador_4x1_8bits_2 (
    .in_1(in_5), .in_2(in_6), .in_3(in_7), .in_4(in_10[1:0]), .in_5(in_8),
    .out_7(multiplexador_4x1_8bits_2_out_7), .in_6(load));
  multiplexador2x1_8bits multiplexador2x1_8bits_1 (
    .in_1(multiplexador_4x1_8bits_1_out_7), .in_2(multiplexador_4x1_8bits_2_out_7), .in_3(in_10[2]),
    .out_5(out_11), .load(load));
endmodule

module multiplexador2x1 (
  input  in_1,
  input  in_2,
  input  load,
  input  in_4,
  output out_5
);

  wire and_1_out, and_2_out, or_1_out;

  and and_1 (and_1_out, in_1, ~in_4);  // AND_Gate
  and and_2 (and_2_out, in_2, in_4);
  or or_1 (or_1_out, and_1_out, and_2_out);
  and and_3 (out_5, or_1_out, load);
endmodule

module multiplexador2x1_8bits (
  input  [7:0] in_1,
  input  [7:0] in_2,
  input  in_3,
  input  load,
  output [7:0] out_5
);

  multiplexador2x1 multiplexador2x1_1 (.in_1(in_1[0]), .in_2(in_2[0]), .out_5(out_5[0]), .in_4(in_3), .load(load));
  multiplexador2x1 multiplexador2x1_2 (.in_1(in_1[1]), .in_2(in_2[1]), .out_5(out_5[1]), .in_4(in_3), .load(load));
  multiplexador2x1 multiplexador2x1_3 (.in_1(in_1[2]), .in_2(in_2[2]), .out_5(out_5[2]), .in_4(in_3), .load(load));
  multiplexador2x1 multiplexador2x1_4 (.in_1(in_1[3]), .in_2(in_2[3]), .out_5(out_5[3]), .in_4(in_3), .load(load));
  multiplexador2x1 multiplexador2x1_5 (.in_1(in_1[4]), .in_2(in_2[4]), .out_5(out_5[4]), .in_4(in_3), .load(load));
  multiplexador2x1 multiplexador2x1_6 (.in_1(in_1[5]), .in_2(in_2[5]), .out_5(out_5[5]), .in_4(in_3), .load(load));
  multiplexador2x1 multiplexador2x1_7 (.in_1(in_1[6]), .in_2(in_2[6]), .out_5(out_5[6]), .in_4(in_3), .load(load));
  multiplexador2x1 multiplexador2x1_8 (.in_1(in_1[7]), .in_2(in_2[7]), .out_5(out_5[7]), .in_4(in_3), .load(load));
endmodule
