// Logisim project 09_detector_sequencia.circ as structural Verilog: 3 circuits, main circuit main
module main (
  input  SET,
  input  RESET,
  input  CLOCK,
  output out_4,
  output out_5,
  output out_6,
  output out_7
);

  wire and_1_out, and_2_out, not_1_out;

  and and_1 (and_1_out, and_2_out, out_4);
  flip_flip_T flip_flip_t_1 (.T(and_1_out), .CLOCK(CLOCK), .SET(SET), .RESET(RESET));  // open: Q, nQ
  and and_2 (and_2_out, out_6, out_5);
  flip_flip_T flip_flip_t_2 (.T(and_2_out), .CLOCK(CLOCK), .SET(SET), .RESET(RESET), .Q(out_4));  // open: nQ
  flip_flip_T flip_flip_t_3 (.T(out_6), .CLOCK(CLOCK), .SET(SET), .RESET(RESET), .Q(out_5));  // open: nQ
  flip_flip_T flip_flip_t_4 (.T(1'b1), .CLOCK(CLOCK), .SET(SET), .RESET(RESET), .Q(out_6));  // open: nQ
  not not_1 (not_1_out, out_5);
  and and_3 (out_7, out_6, not_1_out, out_4);
endmodule

module contador_sincrono (
  input  SET,
  input  RESET,
  input  CLOCK,
  output C,
  output B,
  output A
);

  wire and_1_out, and_2_out;

  and and_1 (and_1_out, and_2_out, C);
  and and_2 (and_2_out, A, B);
  flip_flip_T flip_flip_t_1 (.T(and_1_out), .CLOCK(CLOCK), .SET(SET), .RESET(RESET));  // open: Q, nQ
  flip_flip_T flip_flip_t_2 (.T(and_2_out), .CLOCK(CLOCK), .SET(SET), .RESET(RESET), .Q(C));  // open: nQ
  flip_flip_T flip_flip_t_3 (.T(A), .CLOCK(CLOCK), .SET(SET), .RESET(RESET), .Q(B));  // open: nQ
  flip_flip_T flip_flip_t_4 (.T(1'b1), .CLOCK(CLOCK), .SET(SET), .RESET(RESET), .Q(A));  // open: nQ
endmodule

module flip_flip_T (
  input  SET,
  input  T,
  input  CLOCK,
  input  RESET,
  output Q,
  output nQ
);

  wire nand_1_out, nand_2_out, nand_3_out, nand_4_out, nand_5_out, nand_6_out, not_1_out, not_2_out,
       not_3_out, not_4_out;

  not not_1 (not_1_out, CLOCK);
  nand nand_1 (nand_1_out, nQ, T, not_1_out);
  nand nand_2 (nand_2_out, not_1_out, T, Q);
  not not_2 (not_2_out, SET);
  not not_3 (not_3_out, RESET);
  nand nand_3 (nand_3_out, not_2_out, nand_1_out, nand_4_out);
  not not_4 (not_4_out, not_1_out);
  nand nand_4 (nand_4_out, nand_3_out, nand_2_out, not_3_out);
  nand nand_5 (nand_5_out, nand_3_out, not_3_out, not_4_out);
  nand nand_6 (nand_6_out, not_4_out, not_2_out, nand_4_out);
  nand nand_7 (Q, not_2_out, nand_5_out, nQ);
  nand nand_8 (nQ, Q, nand_6_out, not_3_out);
endmodule
