// Logisim project 10_unidade_logica_aritmetica.circ as structural Verilog: 17 circuits, main circuit main
module main (
  input  [7:0] A,
  input  [7:0] B,
  input  [3:0] SELETOR,
  output [7:0] \SAÍDA 
);

  wire [7:0] AND_out, NAND_out, NOR_out, not_1_out, OR_out, \shift_2bits_dir_1_saída ,
       \shift_2bits_esq_1_saída , \somador_completo_8bits_1_saída , \subtrador_completo_8bits_1_saída ,
       XOR_out;

  assign AND_out = A & B;  // AND_Gate AND, 8 bits wide
  assign OR_out = A | B;  // OR_Gate OR, 8 bits wide
  assign not_1_out = ~A;  // NOT_Gate not_1, 8 bits wide
  assign NOR_out = ~(A | B);  // NOR_Gate NOR, 8 bits wide
  assign NAND_out = ~(A & B);  // NAND_Gate NAND, 8 bits wide
  assign XOR_out = A ^ B;  // XOR_Gate XOR, 8 bits wide
  shift_2bits_esq shift_2bits_esq_1 (.ENTRADA(A), .chave(2'b10), .\SAÍDA (\shift_2bits_esq_1_saída ));
  shift_2bits_dir shift_2bits_dir_1 (.ENTRADA(A), .chave(2'b10), .\SAÍDA (\shift_2bits_dir_1_saída ));
  somador_completo_8bits somador_completo_8bits_1 (
    .ENTRADA(A), .ENTRADA_2(B), .\SAÍDA (\somador_completo_8bits_1_saída ));
  subtrador_completo_8bits subtrador_completo_8bits_1 (
    .ENTRADA(A), .ENTRADA_2(B), .\SAÍDA (\subtrador_completo_8bits_1_saída ));
  multiplex_16x1_8bits MUX (
    .A1(AND_out), .A2(OR_out), .A3(not_1_out), .A4(NOR_out), .A5(NAND_out), .A6(XOR_out),
    .A7(\shift_2bits_esq_1_saída ), .A8(\shift_2bits_dir_1_saída ), .A9(\somador_completo_8bits_1_saída ),
    .A10(\subtrador_completo_8bits_1_saída ), .chave(SELETOR), .\SAÍDA (\SAÍDA ));

  // Notes on the sheet:
  //   NOT
  //   SHIFT A ESQUERDA
  //   SHIFT A DIREITA
  //   SOMADOR
  //   SUBTRADOR
  //   0000 - AND
  //   0001 - OR
  //   0010 - NOT
  //   0011 - NOR
  //   0100 - NAND
  //   0101 - XOR
  //   0110 - SHIFT 2 BITS ESQUERDA
  //   0111 - SHIFT 2 BITS DIREITA
  //   1000 - SOMADOR
  //   1001 - SUBTRADOR
endmodule

module multiplex_4x1 (
  input  in_1,
  input  in_2,
  input  in_3,
  input  in_4,
  input  S2,
  input  S1,
  output out_7
);

  wire and_1_out, and_2_out, and_3_out, and_4_out;

  and and_1 (and_1_out, in_1, ~S2, ~S1);  // AND_Gate
  and and_2 (and_2_out, in_2, ~S2, S1);  // AND_Gate
  and and_3 (and_3_out, in_3, S2, ~S1);  // AND_Gate
  and and_4 (and_4_out, in_4, S2, S1);
  or or_1 (out_7, and_1_out, and_2_out, and_3_out, and_4_out);
endmodule

module multiplex_2x1 (
  input  A,
  input  B,
  input  chave,
  output S
);

  wire and_1_out, and_2_out, not_1_out;

  and and_1 (and_1_out, A, not_1_out);
  not not_1 (not_1_out, chave);
  and and_2 (and_2_out, B, chave);
  or or_1 (S, and_1_out, and_2_out);
endmodule

module multiplex_2x1_8bits (
  input  [7:0] in_1,
  input  [7:0] in_2,
  input  chave,
  output [7:0] out_4
);

  multiplex_2x1 multiplex_2x1_1 (.A(in_1[0]), .B(in_2[0]), .chave(chave), .S(out_4[0]));
  multiplex_2x1 multiplex_2x1_2 (.A(in_1[1]), .B(in_2[1]), .chave(chave), .S(out_4[1]));
  multiplex_2x1 multiplex_2x1_3 (.A(in_1[2]), .B(in_2[2]), .chave(chave), .S(out_4[2]));
  multiplex_2x1 multiplex_2x1_4 (.A(in_1[3]), .B(in_2[3]), .chave(chave), .S(out_4[3]));
  multiplex_2x1 multiplex_2x1_5 (.A(in_1[4]), .B(in_2[4]), .chave(chave), .S(out_4[4]));
  multiplex_2x1 multiplex_2x1_6 (.A(in_1[5]), .B(in_2[5]), .chave(chave), .S(out_4[5]));
  multiplex_2x1 multiplex_2x1_7 (.A(in_1[6]), .B(in_2[6]), .chave(chave), .S(out_4[6]));
  multiplex_2x1 multiplex_2x1_8 (.A(in_1[7]), .B(in_2[7]), .chave(chave), .S(out_4[7]));
endmodule

module multiplex_4x1_8bits (
  input  [7:0] in_1,
  input  [7:0] in_2,
  input  [1:0] chave,
  input  [7:0] in_4,
  input  [7:0] in_5,
  output [7:0] S
);

  multiplex_4x1 multiplex_4x1_1 (
    .in_1(in_1[0]), .in_2(in_2[0]), .in_3(in_4[0]), .in_4(in_5[0]), .S2(chave[1]), .S1(chave[0]), .out_7(S[0]));
  multiplex_4x1 multiplex_4x1_2 (
    .in_1(in_1[1]), .in_2(in_2[1]), .in_3(in_4[1]), .in_4(in_5[1]), .S2(chave[1]), .S1(chave[0]), .out_7(S[1]));
  multiplex_4x1 multiplex_4x1_3 (
    .in_1(in_1[2]), .in_2(in_2[2]), .in_3(in_4[2]), .in_4(in_5[2]), .S2(chave[1]), .S1(chave[0]), .out_7(S[2]));
  multiplex_4x1 multiplex_4x1_4 (
    .in_1(in_1[3]), .in_2(in_2[3]), .in_3(in_4[3]), .in_4(in_5[3]), .S2(chave[1]), .S1(chave[0]), .out_7(S[3]));
  multiplex_4x1 multiplex_4x1_5 (
    .in_1(in_1[4]), .in_2(in_2[4]), .in_3(in_4[4]), .in_4(in_5[4]), .S2(chave[1]), .S1(chave[0]), .out_7(S[4]));
  multiplex_4x1 multiplex_4x1_6 (
    .in_1(in_1[5]), .in_2(in_2[5]), .in_3(in_4[5]), .in_4(in_5[5]), .S2(chave[1]), .S1(chave[0]), .out_7(S[5]));
  multiplex_4x1 multiplex_4x1_7 (
    .in_1(in_1[6]), .in_2(in_2[6]), .in_3(in_4[6]), .in_4(in_5[6]), .S2(chave[1]), .S1(chave[0]), .out_7(S[6]));
  multiplex_4x1 multiplex_4x1_8 (
    .in_1(in_1[7]), .in_2(in_2[7]), .in_3(in_4[7]), .in_4(in_5[7]), .S2(chave[1]), .S1(chave[0]), .out_7(S[7]));
endmodule

module multiplex_8x1_8bits (
  input  [7:0] A0,
  input  [7:0] A1,
  input  [7:0] A2,
  input  [7:0] A3,
  input  [7:0] A4,
  input  [7:0] A5,
  input  [7:0] A6,
  input  [7:0] A7,
  input  [2:0] chave,
  output [7:0] SAIDA
);

  wire [7:0] multiplex_4x1_8bits_1_s, multiplex_4x1_8bits_2_s;

  multiplex_4x1_8bits multiplex_4x1_8bits_1 (
    .in_1(A0), .in_2(A1), .chave(chave[1:0]), .in_4(A2), .in_5(A3), .S(multiplex_4x1_8bits_1_s));
  multiplex_4x1_8bits multiplex_4x1_8bits_2 (
    .in_1(A4), .in_2(A5), .chave(chave[1:0]), .in_4(A6), .in_5(A7), .S(multiplex_4x1_8bits_2_s));
  multiplex_2x1_8bits multiplex_2x1_8bits_1 (
    .in_1(multiplex_4x1_8bits_1_s), .in_2(multiplex_4x1_8bits_2_s), .chave(chave[2]), .out_4(SAIDA));
endmodule

module multiplex_16x1_8bits (
  input  [7:0] A1,
  input  [7:0] A2,
  input  [7:0] A3,
  input  [7:0] A4,
  input  [7:0] A5,
  input  [7:0] A6,
  input  [7:0] A7,
  input  [7:0] A8,
  input  [7:0] A9,
  input  [7:0] A10,
  input  [3:0] chave,
  output [7:0] \SAÍDA 
);

  wire [7:0] MUX_2_saida, MUX_saida;

  multiplex_8x1_8bits MUX (
    .A0(A1), .A1(A2), .A2(A3), .A3(A4), .A4(A5), .A5(A6), .A6(A7), .A7(A8), .chave(chave[2:0]),
    .SAIDA(MUX_saida));
  multiplex_8x1_8bits MUX_2 (
    .A0(A9), .A1(A10), .chave(chave[2:0]), .SAIDA(MUX_2_saida));  // open: A2, A3, A4, A5, A6, A7
  multiplex_2x1_8bits MUX_3 (.in_1(MUX_saida), .in_2(MUX_2_saida), .chave(chave[3]), .out_4(\SAÍDA ));
endmodule

module shift_2bits_esq (
  input  [7:0] ENTRADA,
  input  [1:0] chave,
  output [7:0] \SAÍDA 
);

  wire and_1_out, and_2_out, and_3_out, and_4_out, and_5_out, and_6_out, and_7_out, and_8_out, and_9_out,
       and_10_out, and_11_out, and_12_out, and_13_out, and_14_out, and_15_out, and_17_out, and_18_out,
       and_19_out, and_20_out, and_21_out, and_22_out, and_23_out, and_24_out, and_25_out, and_26_out,
       and_28_out, not_1_out, not_2_out, or_1_out, or_2_out, or_3_out, or_4_out, or_5_out, or_6_out;

  not not_1 (not_1_out, chave[1]);
  and and_1 (and_1_out, ENTRADA[0], chave[1]);
  and and_2 (and_2_out, not_1_out, ENTRADA[1]);
  and and_3 (and_3_out, ENTRADA[1], chave[1]);
  and and_4 (and_4_out, not_1_out, ENTRADA[2]);
  and and_5 (and_5_out, ENTRADA[2], chave[1]);
  and and_6 (and_6_out, not_1_out, ENTRADA[3]);
  and and_7 (and_7_out, ENTRADA[3], chave[1]);
  and and_8 (and_8_out, not_1_out, ENTRADA[4]);
  and and_9 (and_9_out, ENTRADA[4], chave[1]);
  and and_10 (and_10_out, not_1_out, ENTRADA[5]);
  and and_11 (and_11_out, ENTRADA[5], chave[1]);
  and and_12 (and_12_out, not_1_out, ENTRADA[6]);
  and and_13 (and_13_out, ENTRADA[6], chave[1]);
  and and_14 (and_14_out, ENTRADA[7], not_1_out);
  or or_1 (or_1_out, and_5_out, and_8_out);
  or or_2 (or_2_out, and_7_out, and_10_out);
  or or_3 (or_3_out, and_9_out, and_12_out);
  or or_4 (or_4_out, and_11_out, and_14_out);
  or or_5 (or_5_out, and_1_out, and_4_out);
  or or_6 (or_6_out, and_3_out, and_6_out);
  not not_2 (not_2_out, chave[0]);
  and and_15 (and_15_out, and_2_out, not_2_out);
  and and_16 (\SAÍDA [0], chave[0], or_5_out);
  and and_17 (and_17_out, or_5_out, not_2_out);
  and and_18 (and_18_out, chave[0], or_6_out);
  and and_19 (and_19_out, or_6_out, not_2_out);
  and and_20 (and_20_out, chave[0], or_1_out);
  and and_21 (and_21_out, or_1_out, not_2_out);
  and and_22 (and_22_out, chave[0], or_2_out);
  and and_23 (and_23_out, or_2_out, not_2_out);
  and and_24 (and_24_out, chave[0], or_3_out);
  and and_25 (and_25_out, or_3_out, not_2_out);
  and and_26 (and_26_out, chave[0], or_4_out);
  and and_27 (\SAÍDA [7], or_4_out, not_2_out);
  and and_28 (and_28_out, and_13_out, chave[0]);
  or or_7 (\SAÍDA [5], and_23_out, and_26_out);
  or or_8 (\SAÍDA [6], and_25_out, and_28_out);
  or or_9 (\SAÍDA [1], and_15_out, and_18_out);
  or or_10 (\SAÍDA [2], and_17_out, and_20_out);
  or or_11 (\SAÍDA [3], and_19_out, and_22_out);
  or or_12 (\SAÍDA [4], and_21_out, and_24_out);
endmodule

module shift_2bits_dir (
  input  [7:0] ENTRADA,
  input  [1:0] chave,
  output [7:0] \SAÍDA 
);

  wire and_1_out, and_2_out, and_3_out, and_4_out, and_5_out, and_6_out, and_7_out, and_8_out, and_9_out,
       and_10_out, and_11_out, and_12_out, and_13_out, and_14_out, and_15_out, and_17_out, and_18_out,
       and_19_out, and_20_out, and_21_out, and_22_out, and_23_out, and_24_out, and_25_out, and_26_out,
       and_28_out, not_1_out, not_2_out, or_1_out, or_2_out, or_3_out, or_4_out, or_5_out, or_6_out;

  not not_1 (not_1_out, chave[1]);
  and and_1 (and_1_out, ENTRADA[0], not_1_out);
  and and_2 (and_2_out, chave[1], ENTRADA[1]);
  and and_3 (and_3_out, ENTRADA[1], not_1_out);
  and and_4 (and_4_out, chave[1], ENTRADA[2]);
  and and_5 (and_5_out, ENTRADA[2], not_1_out);
  and and_6 (and_6_out, chave[1], ENTRADA[3]);
  and and_7 (and_7_out, ENTRADA[3], not_1_out);
  and and_8 (and_8_out, chave[1], ENTRADA[4]);
  and and_9 (and_9_out, ENTRADA[4], not_1_out);
  and and_10 (and_10_out, chave[1], ENTRADA[5]);
  and and_11 (and_11_out, ENTRADA[5], not_1_out);
  and and_12 (and_12_out, chave[1], ENTRADA[6]);
  and and_13 (and_13_out, ENTRADA[6], not_1_out);
  and and_14 (and_14_out, ENTRADA[7], chave[1]);
  or or_1 (or_1_out, and_5_out, and_8_out);
  or or_2 (or_2_out, and_7_out, and_10_out);
  or or_3 (or_3_out, and_9_out, and_12_out);
  or or_4 (or_4_out, and_11_out, and_14_out);
  or or_5 (or_5_out, and_1_out, and_4_out);
  or or_6 (or_6_out, and_3_out, and_6_out);
  not not_2 (not_2_out, chave[0]);
  and and_15 (and_15_out, and_2_out, chave[0]);
  and and_16 (\SAÍDA [0], not_2_out, or_5_out);
  and and_17 (and_17_out, or_5_out, chave[0]);
  and and_18 (and_18_out, not_2_out, or_6_out);
  and and_19 (and_19_out, or_6_out, chave[0]);
  and and_20 (and_20_out, not_2_out, or_1_out);
  and and_21 (and_21_out, or_1_out, chave[0]);
  and and_22 (and_22_out, not_2_out, or_2_out);
  and and_23 (and_23_out, or_2_out, chave[0]);
  and and_24 (and_24_out, not_2_out, or_3_out);
  and and_25 (and_25_out, or_3_out, chave[0]);
  and and_26 (and_26_out, not_2_out, or_4_out);
  and and_27 (\SAÍDA [7], or_4_out, chave[0]);
  and and_28 (and_28_out, and_13_out, not_2_out);
  or or_7 (\SAÍDA [5], and_23_out, and_26_out);
  or or_8 (\SAÍDA [6], and_25_out, and_28_out);
  or or_9 (\SAÍDA [1], and_15_out, and_18_out);
  or or_10 (\SAÍDA [2], and_17_out, and_20_out);
  or or_11 (\SAÍDA [3], and_19_out, and_22_out);
  or or_12 (\SAÍDA [4], and_21_out, and_24_out);
endmodule

module meio_somador (
  input  A,
  input  B,
  output soma,
  output comp
);

  xor xor_1 (soma, A, B);
  and and_1 (comp, A, B);
endmodule

module somador_completo (
  input  ci,
  input  A,
  input  B,
  output soma,
  output comp
);

  wire meio_somador_1_comp, meio_somador_1_soma, meio_somador_2_comp;

  meio_somador meio_somador_1 (.A(A), .B(B), .soma(meio_somador_1_soma), .comp(meio_somador_1_comp));
  meio_somador meio_somador_2 (.A(ci), .B(meio_somador_1_soma), .soma(soma), .comp(meio_somador_2_comp));
  or or_1 (comp, meio_somador_2_comp, meio_somador_1_comp);
endmodule

module somador_completo_4bits (
  input  C0,
  input  A0,
  input  B0,
  input  A1,
  input  B1,
  input  A2,
  input  B2,
  input  A3,
  input  B3,
  output S0,
  output S1,
  output S2,
  output S3,
  output C4
);

  wire somador_completo_1_comp, somador_completo_2_comp, somador_completo_3_comp;

  somador_completo somador_completo_1 (.ci(C0), .A(A0), .B(B0), .soma(S0), .comp(somador_completo_1_comp));
  somador_completo somador_completo_2 (
    .ci(somador_completo_1_comp), .A(A1), .B(B1), .soma(S1), .comp(somador_completo_2_comp));
  somador_completo somador_completo_3 (
    .ci(somador_completo_2_comp), .A(A2), .B(B2), .soma(S2), .comp(somador_completo_3_comp));
  somador_completo somador_completo_4 (.ci(somador_completo_3_comp), .A(A3), .B(B3), .soma(S3), .comp(C4));
endmodule

module somador_completo_8bits (
  input  [7:0] ENTRADA,
  input  [7:0] ENTRADA_2,
  output [7:0] \SAÍDA 
);

  wire somador_completo_4bits_1_c4, somador_completo_4bits_2_c4;

  somador_completo_4bits somador_completo_4bits_1 (
    .C0(1'b0), .A0(ENTRADA[0]), .B0(ENTRADA_2[0]), .A1(ENTRADA[1]), .B1(ENTRADA_2[1]), .A2(ENTRADA[2]),
    .B2(ENTRADA_2[2]), .A3(ENTRADA[3]), .B3(ENTRADA_2[3]), .S0(\SAÍDA [0]), .S1(\SAÍDA [1]), .S2(\SAÍDA [2]),
    .S3(\SAÍDA [3]), .C4(somador_completo_4bits_1_c4));
  somador_completo_4bits somador_completo_4bits_2 (
    .C0(somador_completo_4bits_1_c4), .A0(ENTRADA[4]), .B0(ENTRADA_2[4]), .A1(ENTRADA[5]), .B1(ENTRADA_2[5]),
    .A2(ENTRADA[6]), .B2(ENTRADA_2[6]), .A3(ENTRADA[7]), .B3(ENTRADA_2[7]), .S0(\SAÍDA [4]), .S1(\SAÍDA [5]),
    .S2(\SAÍDA [6]), .S3(\SAÍDA [7]), .C4(somador_completo_4bits_2_c4));
endmodule

module meio_subtrador (
  input  A,
  input  B,
  output \subtração ,
  output comp
);

  wire not_1_out;

  not not_1 (not_1_out, A);
  xor xor_1 (\subtração , A, B);
  and and_1 (comp, not_1_out, B);
endmodule

module subtrador_completo (
  input  ci,
  input  A,
  input  B,
  output \subtração ,
  output comp
);

  wire meio_subtrador_1_comp, \meio_subtrador_1_subtração , meio_subtrador_2_comp;

  meio_subtrador meio_subtrador_1 (
    .A(A), .B(B), .\subtração (\meio_subtrador_1_subtração ), .comp(meio_subtrador_1_comp));
  meio_subtrador meio_subtrador_2 (
    .A(\meio_subtrador_1_subtração ), .B(ci), .\subtração (\subtração ), .comp(meio_subtrador_2_comp));
  or or_1 (comp, meio_subtrador_2_comp, meio_subtrador_1_comp);
endmodule

module subtrador_completo_4bits (
  input  C0,
  input  A0,
  input  B0,
  input  A1,
  input  B1,
  input  A2,
  input  B2,
  input  A3,
  input  B3,
  output S0,
  output S1,
  output S2,
  output S3,
  output C4
);

  wire subtrador_completo_1_comp, subtrador_completo_2_comp, subtrador_completo_3_comp;

  subtrador_completo subtrador_completo_1 (.ci(C0), .A(A0), .B(B0), .\subtração (S0), .comp(subtrador_completo_1_comp));
  subtrador_completo subtrador_completo_2 (
    .ci(subtrador_completo_1_comp), .A(A1), .B(B1), .\subtração (S1), .comp(subtrador_completo_2_comp));
  subtrador_completo subtrador_completo_3 (
    .ci(subtrador_completo_2_comp), .A(A2), .B(B2), .\subtração (S2), .comp(subtrador_completo_3_comp));
  subtrador_completo subtrador_completo_4 (.ci(subtrador_completo_3_comp), .A(A3), .B(B3), .\subtração (S3), .comp(C4));
endmodule

module subtrador_completo_8bits (
  input  [7:0] ENTRADA,
  input  [7:0] ENTRADA_2,
  output [7:0] \SAÍDA 
);

  wire subtrador_completo_4bits_1_c4, subtrador_completo_4bits_2_c4;

  subtrador_completo_4bits subtrador_completo_4bits_1 (
    .C0(1'b0), .A0(ENTRADA[0]), .B0(ENTRADA_2[0]), .A1(ENTRADA[1]), .B1(ENTRADA_2[1]), .A2(ENTRADA[2]),
    .B2(ENTRADA_2[2]), .A3(ENTRADA[3]), .B3(ENTRADA_2[3]), .S0(\SAÍDA [0]), .S1(\SAÍDA [1]), .S2(\SAÍDA [2]),
    .S3(\SAÍDA [3]), .C4(subtrador_completo_4bits_1_c4));
  subtrador_completo_4bits subtrador_completo_4bits_2 (
    .C0(subtrador_completo_4bits_1_c4), .A0(ENTRADA[4]), .B0(ENTRADA_2[4]), .A1(ENTRADA[5]),
    .B1(ENTRADA_2[5]), .A2(ENTRADA[6]), .B2(ENTRADA_2[6]), .A3(ENTRADA[7]), .B3(ENTRADA_2[7]),
    .S0(\SAÍDA [4]), .S1(\SAÍDA [5]), .S2(\SAÍDA [6]), .S3(\SAÍDA [7]), .C4(subtrador_completo_4bits_2_c4));
endmodule
