// Logisim project 11_extensor de sinal_4_8.circ as structural Verilog: 1 circuit, main circuit main
module main (
  input  [3:0] Entrada,
  input  \Tipo_de_saída_de_extensão ,
  output [7:0] Sinal_final
);


  assign Sinal_final = {{4{\Tipo_de_saída_de_extensão }}, Entrada};
endmodule
