// Logisim project 12_maquina_estados.circ as structural Verilog: 3 circuits, main circuit main
module main (
  input  X,
  input  SET,
  input  RESET,
  output Y
);

  wire and_1_out, and_2_out, clock_1_out, flipflopt_1_q, flipflopt_2_q, or_1_out;

  and and_1 (and_1_out, flipflopt_1_q, X, ~flipflopt_2_q);  // AND_Gate
  and and_2 (and_2_out, flipflopt_2_q, ~X);  // AND_Gate
  or or_1 (or_1_out, and_1_out, and_2_out);
  Clock clock_1 (.out(clock_1_out));
  flipflopT flipflopt_1 (.T(or_1_out), .CLOCK(clock_1_out), .Q(flipflopt_1_q), .SET(SET), .RESET(RESET));  // open: nQ
  flipflopT flipflopt_2 (.T(X), .CLOCK(clock_1_out), .Q(flipflopt_2_q), .SET(SET), .RESET(RESET));  // open: nQ
  and and_3 (Y, flipflopt_1_q, flipflopt_2_q);
endmodule

module flipflopD (
  input  in_1,
  input  in_2,
  output Q,
  output nQ
);

  wire and_1_out, and_2_out, not_1_out;

  not not_1 (not_1_out, in_2);
  and and_1 (and_1_out, in_1, not_1_out);
  and and_2 (and_2_out, in_2, in_1);
  nor nor_1 (Q, and_1_out, nQ);
  nor nor_2 (nQ, Q, and_2_out);
endmodule

module flipflopT (
  input  SET,
  input  T,
  input  CLOCK,
  input  RESET,
  output Q,
  output nQ
);

  wire nand_1_out, nand_2_out, nand_3_out, nand_4_out, nand_5_out, nand_6_out, not_1_out, not_2_out,
       not_3_out, not_4_out;

  not not_1 (not_1_out, T);
  nand nand_1 (nand_1_out, nQ, T, CLOCK);
  nand nand_2 (nand_2_out, CLOCK, not_1_out, Q);
  not not_2 (not_2_out, SET);
  not not_3 (not_3_out, RESET);
  nand nand_3 (nand_3_out, not_2_out, nand_1_out, nand_4_out);
  not not_4 (not_4_out, CLOCK);
  nand nand_4 (nand_4_out, nand_3_out, nand_2_out, not_3_out);
  nand nand_5 (nand_5_out, nand_3_out, not_3_out, not_4_out);
  nand nand_6 (nand_6_out, not_4_out, not_2_out, nand_4_out);
  nand nand_7 (Q, not_2_out, nand_5_out, nQ);
  nand nand_8 (nQ, Q, nand_6_out, not_3_out);
endmodule
