// Logisim project 15_circuito_karnaugh.circ as structural Verilog: 1 circuit, main circuit main
module main (
  input  A,
  input  B,
  input  C,
  input  A2,
  input  B2,
  input  C2,
  output S,
  output SO
);

  wire and_1_out, and_2_out, and_3_out, and_4_out, and_5_out, and_6_out, not_1_out, not_2_out, not_3_out,
       not_4_out, not_5_out;

  not not_1 (not_1_out, A);
  not not_2 (not_2_out, B);
  not not_3 (not_3_out, C);
  and and_1 (and_1_out, not_1_out, not_2_out, not_3_out);
  and and_2 (and_2_out, not_1_out, not_2_out, C);
  and and_3 (and_3_out, not_1_out, B, C);
  and and_4 (and_4_out, A, not_2_out, C);
  and and_5 (and_5_out, A, B, C);
  or or_1 (S, and_1_out, and_2_out, and_3_out, and_4_out, and_5_out);
  not not_4 (not_4_out, A2);
  not not_5 (not_5_out, B2);
  and and_6 (and_6_out, not_4_out, not_5_out);
  or or_2 (SO, and_6_out, C2);
endmodule
