// Logisim project 1_flip_flop_D.circ as structural Verilog: 1 circuit, main circuit main
module main (
  input  D,
  output Q,
  output nQ
);

  wire and_1_out, and_2_out, CLOCK_out, not_1_out;

  not not_1 (not_1_out, D);
  Clock CLOCK (.out(CLOCK_out));
  and and_1 (and_1_out, CLOCK_out, not_1_out);
  and and_2 (and_2_out, D, CLOCK_out);
  nor nor_1 (Q, and_1_out, nQ);
  nor nor_2 (nQ, Q, and_2_out);
endmodule
