// Logisim project 4_somador_de_4_com_inteiro.circ as structural Verilog: 2 circuits, main circuit main
module main (
  input  AO,
  input  Cin,
  input  A1,
  input  A2,
  input  A3,
  input  A4,
  input  A5,
  input  A6,
  input  A7,
  output S0,
  output S1,
  output S2,
  output S3,
  output S4,
  output S5,
  output S6,
  output S7,
  output Cout
);

  wire somador_1_bit_1_cout, somador_1_bit_2_cout, somador_1_bit_3_cout, somador_1_bit_4_cout,
       somador_1_bit_5_cout, somador_1_bit_6_cout, somador_1_bit_7_cout;

  somador_1_bit somador_1_bit_1 (.A(AO), .B(1'b0), .Cin(Cin), .S(S0), .Cout(somador_1_bit_1_cout));
  somador_1_bit somador_1_bit_2 (.A(A1), .B(1'b0), .Cin(somador_1_bit_1_cout), .S(S1), .Cout(somador_1_bit_2_cout));
  somador_1_bit somador_1_bit_3 (.A(A2), .B(1'b1), .Cin(somador_1_bit_2_cout), .S(S2), .Cout(somador_1_bit_3_cout));
  somador_1_bit somador_1_bit_4 (.A(A3), .B(1'b0), .Cin(somador_1_bit_3_cout), .S(S3), .Cout(somador_1_bit_4_cout));
  somador_1_bit somador_1_bit_5 (.A(A4), .B(1'b0), .Cin(somador_1_bit_4_cout), .S(S4), .Cout(somador_1_bit_5_cout));
  somador_1_bit somador_1_bit_6 (.A(A5), .B(1'b0), .Cin(somador_1_bit_5_cout), .S(S5), .Cout(somador_1_bit_6_cout));
  somador_1_bit somador_1_bit_7 (.A(A6), .B(1'b0), .Cin(somador_1_bit_6_cout), .S(S6), .Cout(somador_1_bit_7_cout));
  somador_1_bit somador_1_bit_8 (.A(A7), .B(1'b0), .Cin(somador_1_bit_7_cout), .S(S7), .Cout(Cout));
endmodule

module somador_1_bit (
  input  A,
  input  B,
  input  Cin,
  output S,
  output Cout
);

  wire and_1_out, and_2_out, and_3_out, xor_1_out;

  xor xor_1 (xor_1_out, A, B);
  and and_1 (and_1_out, A, B);
  and and_2 (and_2_out, A, Cin);
  and and_3 (and_3_out, B, Cin);
  xor xor_2 (S, xor_1_out, Cin);
  or or_1 (Cout, and_1_out, and_2_out, and_3_out);
endmodule
