// Logisim project 8_somador_8bits.circ as structural Verilog: 4 circuits, main circuit somador_completo(8bits)
module meio_somador (
  input  A,
  input  B,
  output soma,
  output comp
);

  xor xor_1 (soma, A, B);
  and and_1 (comp, A, B);
endmodule

module somador_completo (
  input  ci,
  input  A,
  input  B,
  output soma,
  output comp
);

  wire meio_somador_1_comp, meio_somador_1_soma, meio_somador_2_comp;

  meio_somador meio_somador_1 (.A(A), .B(B), .soma(meio_somador_1_soma), .comp(meio_somador_1_comp));
  meio_somador meio_somador_2 (.A(ci), .B(meio_somador_1_soma), .soma(soma), .comp(meio_somador_2_comp));
  or or_1 (comp, meio_somador_2_comp, meio_somador_1_comp);
endmodule

module somador_completo_4bits (
  input  C0,
  input  A0,
  input  B0,
  input  A1,
  input  B1,
  input  A2,
  input  B2,
  input  A3,
  input  B3,
  output S0,
  output S1,
  output S2,
  output S3,
  output C4
);

  wire somador_completo_1_comp, somador_completo_2_comp, somador_completo_3_comp;

  somador_completo somador_completo_1 (.ci(C0), .A(A0), .B(B0), .soma(S0), .comp(somador_completo_1_comp));
  somador_completo somador_completo_2 (
    .ci(somador_completo_1_comp), .A(A1), .B(B1), .soma(S1), .comp(somador_completo_2_comp));
  somador_completo somador_completo_3 (
    .ci(somador_completo_2_comp), .A(A2), .B(B2), .soma(S2), .comp(somador_completo_3_comp));
  somador_completo somador_completo_4 (.ci(somador_completo_3_comp), .A(A3), .B(B3), .soma(S3), .comp(C4));
endmodule

module somador_completo_8bits (
  input  Cin,
  input  [7:0] ENTRADA,
  input  [7:0] ENTRADA_2,
  output [7:0] \SAÍDA ,
  output Cout
);

  wire somador_completo_4bits_1_c4;

  somador_completo_4bits somador_completo_4bits_1 (
    .C0(Cin), .A0(ENTRADA[0]), .B0(ENTRADA_2[0]), .A1(ENTRADA[1]), .B1(ENTRADA_2[1]), .A2(ENTRADA[2]),
    .B2(ENTRADA_2[2]), .A3(ENTRADA[3]), .B3(ENTRADA_2[3]), .S0(\SAÍDA [0]), .S1(\SAÍDA [1]), .S2(\SAÍDA [2]),
    .S3(\SAÍDA [3]), .C4(somador_completo_4bits_1_c4));
  somador_completo_4bits somador_completo_4bits_2 (
    .C0(somador_completo_4bits_1_c4), .A0(ENTRADA[4]), .B0(ENTRADA_2[4]), .A1(ENTRADA[5]), .B1(ENTRADA_2[5]),
    .A2(ENTRADA[6]), .B2(ENTRADA_2[6]), .A3(ENTRADA[7]), .B3(ENTRADA_2[7]), .S0(\SAÍDA [4]), .S1(\SAÍDA [5]),
    .S2(\SAÍDA [6]), .S3(\SAÍDA [7]), .C4(Cout));
endmodule
